# Fritzing sketch SamplingCircuit (saved by Fritzing 1.0.2b)

parts:
  U1 = MEMS  # not connected
  U2 = PSoC 5LP
  U1_2 = ESP32S3

nets:
  GND: U2.GND, U1_2.GND
  N1: U2.P2_0, U1_2.GPIO10
  N2: U2.P2_1, U1_2.GPIO11
  N3: U2.P2_2, U1_2.GPIO12, U1_2.GPIO36, U1_2.GPIO42
  N4: U2.P2_3, U1_2.GPIO13
  N5: U2.VDDIO, U1_2.3.3

custom parts:
  MEMS: Mems mic
  ESP32S3: s3
